# Fritzing sketch projekt (saved by Fritzing 0.9.3b)
circuit board: 5.58612cm x 6.09505cm
breadboards: 1

parts:
  U2 = NodeMCU V1.0
  mq135 = MQ-3 breakout
  DHT11 = DHT11 Humitidy and Temperature Sensor
  LED1 = smd LED [color="Green (570nm)" package="0805 [SMD]"]
  LED2 = smd LED [color="Yellow (595nm)" package="0805 [SMD]"]
  LED3 = smd LED [color="Red (633nm)" package="0805 [SMD]"]
  R3 = Resistor [tolerance=±5% resistance=220 package="0402 [SMD]"]
  R2 = Resistor [tolerance=±5% resistance=220 package="0402 [SMD]"]
  R1 = Resistor [tolerance=±5% resistance=220 package="0402 [SMD]"]

nets:
  N1: U2.D1, DHT11.DATA
  N2: U2.D2, R3.Pin_0
  3V3: U2.3V3, DHT11.VDD
  GND: U2.GND, mq135.GND, DHT11.GND, LED1.cathode, LED2.cathode, LED3.cathode
  N3: U2.D5, R2.Pin_0
  N4: U2.D6, R1.Pin_0
  N5: U2.RSV, mq135.VCC
  N6: U2.A0, mq135.AO
  N7: LED1.anode, R1.Pin_1
  N8: LED2.anode, R2.Pin_1
  N9: LED3.anode, R3.Pin_1

custom parts:
  NodeMCU V1.0: ESP8266 based NodeMCU
  MQ-3 breakout: Alcohol sensor is capable of detecting alcohol (ethanol) particles on itself and gives the information in digital form back to us to manipulate with it. SKU:101251 • Voltage: 5V DC • Power: max 750mW • Measurement range: 0.04-4mg/L
  DHT11 Humitidy and Temperature Sensor: DHT11 Humidity and Temperature Sensor
